# Fritzing sketch Blink_Led (saved by Fritzing 0.9.10b)
breadboards: 1

parts:
  LED1 = smd LED [color="Red (633nm)" package="1206 [SMD]"]
  R1 = Resistor [tolerance=±5% resistance=220 package="2010 [SMD]"]
  A1 = Arduino R4 Minima

nets:
  N1: LED1.cathode, A1.Pin_17, A1.Pin_45
  N2: LED1.anode, R1.Pin_0
  N3: R1.Pin_1, A1.Pin_31, A1.Pin_32, A1.Pin_33, A1.Pin_34, A1.Pin_35, A1.Pin_36, A1.Pin_37

custom parts:
  Arduino R4 Minima: Introducing the Arduino UNO R4 Minima! This board boasts the RA4M1 microprocessor from Renesas, delivering increased processing power, expanded memory, and additional peripherals.
